# Fritzing sketch IRControlReceive (saved by Fritzing 0.9.3b)
breadboards: 1

parts:
  Part1 = Arduino Nano (Rev3.0)
  R1 = Resistor [tolerance=±5% resistance=1k package="0402 [SMD]"]

nets:
  N1: Part1.D11/MOSI, R1.Pin_0
  N2: Part1.5V, R1.Pin_1

notes:
  IR receptor
